// Digital circuit 8bits_subtractor.dig as structural Verilog
module _8bits_subtractor (
  input  [7:0] in_2,
  input  in_3,
  input  [7:0] in_4,
  output [7:0] D,
  output F
);

  wire [7:0] _8bits_adder_1_s, not_1_out;

  assign not_1_out = ~in_2;  // Not not_1, 8 bits wide
  _8bits_adder _8bits_adder_1 (.A(in_4), .B(not_1_out), .C(in_3), .S(_8bits_adder_1_s), .C_o(F));
  _8bits_adder _8bits_adder_2 (.A(_8bits_adder_1_s), .B(8'h1), .C(1'b0), .S(D));  // open: C_o

  // Notes on the sheet:
  //   in_2: default 11
  //   in_4: default 5
endmodule
