// Digital circuit 8bits_adder.dig as structural Verilog
module _8bits_adder (
  input  [7:0] A,
  input  [7:0] B,
  input  C,
  output [7:0] S,
  output C_o
);

  wire full_adder_1_c_o, full_adder_2_c_o, full_adder_3_c_o, full_adder_4_c_o, full_adder_5_c_o,
       full_adder_6_c_o, full_adder_7_c_o;

  full_adder full_adder_1 (.A(A[0]), .B(B[0]), .C_i(C), .S(S[0]), .C_o(full_adder_1_c_o));
  full_adder full_adder_2 (.A(A[4]), .B(B[4]), .C_i(full_adder_7_c_o), .S(S[4]), .C_o(full_adder_2_c_o));
  full_adder full_adder_3 (.A(A[1]), .B(B[1]), .C_i(full_adder_1_c_o), .S(S[1]), .C_o(full_adder_3_c_o));
  full_adder full_adder_4 (.A(A[5]), .B(B[5]), .C_i(full_adder_2_c_o), .S(S[5]), .C_o(full_adder_4_c_o));
  full_adder full_adder_5 (.A(A[2]), .B(B[2]), .C_i(full_adder_3_c_o), .S(S[2]), .C_o(full_adder_5_c_o));
  full_adder full_adder_6 (.A(A[6]), .B(B[6]), .C_i(full_adder_4_c_o), .S(S[6]), .C_o(full_adder_6_c_o));
  full_adder full_adder_7 (.A(A[3]), .B(B[3]), .C_i(full_adder_5_c_o), .S(S[3]), .C_o(full_adder_7_c_o));
  full_adder full_adder_8 (.A(A[7]), .B(B[7]), .C_i(full_adder_6_c_o), .S(S[7]), .C_o(C_o));
endmodule

/* Test case:
A B C S C_{o}
2 2 0 4 0
*/
