// Digital circuit 8bits_multiplier.dig as structural Verilog
module _8bits_multiplier (
  input  [7:0] A,
  input  [7:0] B,
  output [7:0] M,
  output O_F
);

  wire _8bits_adder_1_p5, _8bits_adder_2_c_o, _8bits_adder_3_c_o, _8bits_adder_4_c_o, _8bits_adder_5_c_o,
       _8bits_adder_6_c_o, _8bits_adder_7_c_o, INIT, or_2_out, Overflow_Check;
  wire [7:0] _8bits_adder_1_p4, _8bits_adder_2_s, _8bits_adder_3_s, _8bits_adder_4_s, _8bits_adder_5_s,
       _8bits_adder_6_s;
  wire [7:1] bit1, multiply_check_helper_8_p3;
  wire [7:2] bit2, multiply_check_helper_7_p3;
  wire [7:3] bit3, multiply_check_helper_6_p3;
  wire [7:4] bit4, multiply_check_helper_5_p3;
  wire [7:5] bit5, multiply_check_helper_4_p3;
  wire [7:6] bit6, multiply_check_helper_3_p3;
  wire [7:7] bit7, multiply_check_helper_2_p3;

  // multiply_check_helper multiply_check_helper_1: pin names not known; wires that end beside it: A, B[0], INIT
  // multiply_check_helper multiply_check_helper_2: pin names not known; wires that end beside it: A, B[1], {multiply_check_helper_2_p3[7], bit1}
  // multiply_check_helper multiply_check_helper_3: pin names not known; wires that end beside it: A, B[2], {multiply_check_helper_3_p3, bit2}
  // multiply_check_helper multiply_check_helper_4: pin names not known; wires that end beside it: A, B[3], {multiply_check_helper_4_p3, bit3}
  // multiply_check_helper multiply_check_helper_5: pin names not known; wires that end beside it: A, B[4], {multiply_check_helper_5_p3, bit4}
  // multiply_check_helper multiply_check_helper_6: pin names not known; wires that end beside it: A, B[5], {multiply_check_helper_6_p3, bit5}
  // multiply_check_helper multiply_check_helper_7: pin names not known; wires that end beside it: A, B[6], {multiply_check_helper_7_p3, bit6}
  // multiply_check_helper multiply_check_helper_8: pin names not known; wires that end beside it: A, B[7], {multiply_check_helper_8_p3, bit7[7]}
  // _8bits_adder _8bits_adder_1: pin names not known; wires that end beside it: INIT, {bit1, 1'b0}, 1'b0, _8bits_adder_1_p4, _8bits_adder_1_p5
  _8bits_adder _8bits_adder_2 (
    .A(_8bits_adder_1_p4), .B({bit2, 2'b00}), .C(1'b0), .S(_8bits_adder_2_s), .C_o(_8bits_adder_2_c_o));
  _8bits_adder _8bits_adder_3 (
    .A(_8bits_adder_2_s), .B({bit3, 3'b000}), .C(1'b0), .S(_8bits_adder_3_s), .C_o(_8bits_adder_3_c_o));
  _8bits_adder _8bits_adder_4 (
    .A(_8bits_adder_3_s), .B({bit4, 4'b0000}), .C(1'b0), .S(_8bits_adder_4_s), .C_o(_8bits_adder_4_c_o));
  or or_1 (Overflow_Check, _8bits_adder_1_p5, _8bits_adder_2_c_o, _8bits_adder_3_c_o, _8bits_adder_4_c_o, _8bits_adder_5_c_o, _8bits_adder_6_c_o, _8bits_adder_7_c_o);
  _8bits_adder _8bits_adder_5 (
    .A(_8bits_adder_4_s), .B({bit5, {5{1'b0}}}), .C(1'b0), .S(_8bits_adder_5_s), .C_o(_8bits_adder_5_c_o));
  _8bits_adder _8bits_adder_6 (
    .A(_8bits_adder_5_s), .B({bit6, {6{1'b0}}}), .C(1'b0), .S(_8bits_adder_6_s), .C_o(_8bits_adder_6_c_o));
  _8bits_adder _8bits_adder_7 (
    .A(_8bits_adder_6_s), .B({bit7[7], {7{1'b0}}}), .C(1'b0), .S(M), .C_o(_8bits_adder_7_c_o));
  or or_2 (or_2_out, multiply_check_helper_2_p3[7], multiply_check_helper_3_p3[6], multiply_check_helper_3_p3[7], multiply_check_helper_4_p3[5], multiply_check_helper_4_p3[6], multiply_check_helper_4_p3[7], multiply_check_helper_5_p3[4], multiply_check_helper_5_p3[5], multiply_check_helper_5_p3[6], multiply_check_helper_5_p3[7], multiply_check_helper_6_p3[3], multiply_check_helper_6_p3[4], multiply_check_helper_6_p3[5], multiply_check_helper_6_p3[6], multiply_check_helper_6_p3[7], multiply_check_helper_7_p3[2], multiply_check_helper_7_p3[3], multiply_check_helper_7_p3[4], multiply_check_helper_7_p3[5], multiply_check_helper_7_p3[6], multiply_check_helper_7_p3[7], multiply_check_helper_8_p3[1], multiply_check_helper_8_p3[2], multiply_check_helper_8_p3[3], multiply_check_helper_8_p3[4], multiply_check_helper_8_p3[5], multiply_check_helper_8_p3[6], multiply_check_helper_8_p3[7]);
  or or_3 (O_F, Overflow_Check, or_2_out);
endmodule

/* Test case:
A	B	M	O_{F}
4	100	144	1
*/
