// Digital circuit 8bits_register.dig as structural Verilog
module _8bits_register (
  input  [7:0] D,
  input  CLK,
  output [7:0] Q
);

  D_flip_flop _0 (.D(D[0]), .CLK(CLK), .Q(Q[0]));  // open: Q_2
  D_flip_flop _4 (.D(D[4]), .CLK(CLK), .Q(Q[4]));  // open: Q_2
  D_flip_flop _1 (.D(D[1]), .CLK(CLK), .Q(Q[1]));  // open: Q_2
  D_flip_flop _5 (.D(D[5]), .CLK(CLK), .Q(Q[5]));  // open: Q_2
  D_flip_flop _2 (.D(D[2]), .CLK(CLK), .Q(Q[2]));  // open: Q_2
  D_flip_flop _6 (.D(D[6]), .CLK(CLK), .Q(Q[6]));  // open: Q_2
  D_flip_flop _3 (.D(D[3]), .CLK(CLK), .Q(Q[3]));  // open: Q_2
  D_flip_flop _7 (.D(D[7]), .CLK(CLK), .Q(Q[7]));  // open: Q_2
endmodule
