// Digital circuit ALU.dig as structural Verilog
module ALU (
  input  [7:0] A,
  input  [7:0] B,
  input  [1:0] Do_Math,
  input  CLK,
  output [7:0] Result,
  output NegFlag,
  output ZeroFlag,
  output OverflowFlag,
  output [7:0] Debug
);

  wire _8bits_adder_1_c_o, ADD, and_1_out, and_2_out, demultiplexer_1_out_2, demultiplexer_5_out_0,
       multiplier_1_o_f, nor_1_out, not_2_out, not_4_out, not_5_out, or_1_out, Sub;
  wire [7:0] _8bits_adder_1_s, _8bits_adder_2_s, demultiplexer_2_out_0, demultiplexer_2_out_1,
       demultiplexer_3_out_0, demultiplexer_3_out_1, demultiplexer_4_out_0, demultiplexer_4_out_1, M_Result,
       multiplexer_1_out, multiplexer_2_out, multiplexer_3_out, not_1_out, not_3_out;

  Demultiplexer #(.Selector_Bits(2)) demultiplexer_1 (
    .sel(Do_Math), .in(CLK), .out_0(ADD), .out_1(Sub), .out_2(demultiplexer_1_out_2));  // open: out_3
  Demultiplexer #(.Bits(8)) demultiplexer_2 (
    .sel(Sub), .in(B), .out_0(demultiplexer_2_out_0), .out_1(demultiplexer_2_out_1));
  assign not_1_out = ~demultiplexer_2_out_1;  // Not not_1, 8 bits wide
  Multiplexer #(.Bits(8)) multiplexer_1 (
    .sel(Sub), .in_0(demultiplexer_2_out_0), .in_1(not_1_out), .out(multiplexer_1_out));
  multiplier multiplier_1 (
    .A(A), .CLK(demultiplexer_1_out_2), .B(B), .EN(not_2_out), .M(M_Result), .O_F(multiplier_1_o_f),
    .countOut(Debug));
  not not_2 (not_2_out, multiplier_1_o_f);
  _8bits_adder _8bits_adder_1 (.A(A), .B(multiplexer_1_out), .C(1'b0), .S(_8bits_adder_1_s), .C_o(_8bits_adder_1_c_o));
  Demultiplexer #(.Bits(8)) demultiplexer_3 (
    .sel(Sub), .in(_8bits_adder_1_s), .out_0(demultiplexer_3_out_0), .out_1(demultiplexer_3_out_1));
  Demultiplexer #(.Bits(8)) demultiplexer_4 (
    .sel(_8bits_adder_1_c_o), .in(demultiplexer_3_out_1), .out_0(demultiplexer_4_out_0),
    .out_1(demultiplexer_4_out_1));
  assign not_3_out = ~demultiplexer_4_out_0;  // Not not_3, 8 bits wide
  not not_4 (not_4_out, Sub);
  _8bits_adder _8bits_adder_2 (
    .A(demultiplexer_4_out_1), .B({8{1'b0}}), .C(_8bits_adder_1_c_o), .S(_8bits_adder_2_s));  // open: C_o
  and and_1 (and_1_out, _8bits_adder_1_c_o, not_4_out);
  Multiplexer #(.Bits(8)) multiplexer_2 (
    .sel(_8bits_adder_1_c_o), .in_0(not_3_out), .in_1(_8bits_adder_2_s), .out(multiplexer_2_out));
  Multiplexer #(.Bits(8)) multiplexer_3 (
    .sel(Sub), .in_0(demultiplexer_3_out_0), .in_1(multiplexer_2_out), .out(multiplexer_3_out));
  not not_5 (not_5_out, _8bits_adder_1_c_o);
  Multiplexer multiplexer_4 (.sel(ADD), .in_0(multiplier_1_o_f), .in_1(and_1_out), .out(OverflowFlag));
  or or_1 (or_1_out, ADD, Sub);
  and and_2 (and_2_out, Sub, not_5_out);
  Multiplexer #(.Bits(8)) multiplexer_5 (.sel(or_1_out), .in_0(M_Result), .in_1(multiplexer_3_out), .out(Result));
  nor nor_1 (nor_1_out, multiplexer_3_out[0], multiplexer_3_out[1], multiplexer_3_out[2], multiplexer_3_out[3], multiplexer_3_out[4], multiplexer_3_out[5], multiplexer_3_out[6], multiplexer_3_out[7]);
  Demultiplexer demultiplexer_5 (.sel(ZeroFlag), .in(and_2_out), .out_0(demultiplexer_5_out_0));  // open: out_1
  Multiplexer multiplexer_6 (.sel(CLK), .in_0(1'b0), .in_1(nor_1_out), .out(ZeroFlag));
  Multiplexer multiplexer_7 (.sel(ZeroFlag), .in_0(demultiplexer_5_out_0), .in_1(1'b0), .out(NegFlag));

  // Notes on the sheet:
  //   A: default 4
  //   B: default 100
  //   Do_Math: default 2
endmodule

/* Test case:
A	B	Do_{Math}	OverflowFlag	NegFlag	ZeroFlag	Result	CLK
2	5	1		0		0	0		0	0
2	5	1		0		1	0		3	1
250	15	0		0		0	0		0	0
250	15	0		1		0	0		9	1
50	50	1		0		0	0		0	0
50	50	1		0		0	1		0	1
0	0	0		0		0	0		0	0
0	0	0		0		0	1		0	1
255	1	0		0		0	0		0	0
255	1	0		1		0	1		0	1
4	100	2		0		0	0		0	0
4	100	2		0		0	0		0	1
4	100	2		0		0	0		0	0
4	100	2		1		0	0		0	1
4	100	2		1		0	0		0	0
4	100	2		0		0	0		0	1
2	3	2		0		0	0		0	0
2	3	2		0		0	0		0	1
2	3	2		0		0	0		0	0
2	3	2		0		0	0		6	1
*/
