// Digital circuit CPU_OLD.dig as structural Verilog
module CPU_OLD (
  input  CLK,
  input  [7:0] Input_8Bits,
  input  in_7,
  input  in_8,
  input  in_9,
  output [7:0] Output_8Bits,
  output [7:0] out_4,
  output [7:0] out_5,
  output [7:0] out_6,
  output [11:0] out_10,
  output [11:0] out_11,
  output [11:0] out_12,
  output Stack_OVERSIZE,
  output Stack_EMPTY
);

  wire and_1_out, and_3_out, and_5_out, and_6_out, and_7_out, Branching_SetUp_q, CLK_t, comparator_1_eq,
       comparator_2_eq, comparator_4_lt, comparator_6_eq, counterpreset_1_ovf, EX_Do_Branch_Taking,
       EX_Do_Jump, EX_DO_Stack, EX_IMM_check, EX_Jump_EN, EX_Math_EN, EX_Mem_EN, EX_Mov_EN, EX_NO_NOP,
       EX_NOP_Out, ID_IMM_check, ME_DelayNOP, ME_Do_LD, ME_Do_POP, ME_Do_PSH, ME_Do_RD, ME_Do_ST, ME_Do_WR,
       multiplexer_3_out, multiplexer_7_out, multiplexer_8_out, multiplexer_21_out, not_4_out, not_5_out,
       not_6_out, not_7_out, not_8_out, not_9_out, not_10_out, not_13_out, not_14_out, not_15_out,
       not_16_out, not_18_out, not_19_out, NotNOPing, or_2_out, or_3_out, or_6_out, or_7_out, or_8_out,
       register_5_q, register_6_q, register_8_q, register_9_q, register_10_q, register_12_q, WB_NO_NOP;
  wire [1:0] counter_1_out, EX_Do_SMTH, multiplexer_4_out, not_2_out, not_3_out;
  wire [2:0] EX_ALU_Choice_01, EX_ALU_Choice_10, EX_R_Dest, EX_R_Src1, EX_R_Src2, ID_R_Dest, ID_R_Src1,
       ID_R_Src2, ME_R_DestOut, ME_R_Src2, multiplexer_10_out, multiplexer_14_out, register_1_q;
  wire [3:0] ALU_c_f, EX_Reg_F;
  wire [4:0] ID_Opcode, multiplexer_12_out;
  wire [5:0] rom_1_d;
  wire [7:0] ALU_res, EX_ALU_Out, EX_Data_A, EX_Data_B, EX_Forward_A, EX_Forward_B, EX_ME_Stack_Addr,
       EX_ME_Stack_Out, ID_Data_A, ID_Data_B, ID_StackPtr_Out, ME_LD_ST_output, ME_RD_WR_output,
       multiplexer_1_out, multiplexer_2_out, multiplexer_13_out, multiplexer_20_out, R_Src_2_Out,
       register_3_q, register_4_q;
  wire [7:3] ID_R_Src2_IMM;
  wire [8:0] ID_EX_Stack_Out;
  wire [12:0] ME_WB_Out;
  wire [15:0] EX_ME_Forward_Out, multiplexer_9_out;
  wire [17:0] PSH_POP_CMD;
  wire [18:0] LD_ST_CMD, multiplexer_5_out;
  wire [19:0] Instruction_d;
  wire [24:24] ID_EX_Out;
  wire [25:0] EX_ME_Out, multiplexer_19_out, register_11_q;

  or or_1 (CLK_t, CLK, in_9, in_8, in_7);
  CounterPreset #(.Bits(8)) counterpreset_1 (
    .en(NotNOPing), .C(CLK_t), .dir(1'b0), .in(EX_Data_B), .ld(EX_Do_Branch_Taking),
    .clr(counterpreset_1_ovf), .out(out_4), .ovf(counterpreset_1_ovf));
  nand nand_1 (NotNOPing, not_4_out, or_3_out);
  or or_2 (or_2_out, EX_Do_Branch_Taking, comparator_1_eq);
  or or_3 (or_3_out, multiplexer_3_out, EX_Do_Branch_Taking);
  Register Branching_SetUp (.D(or_3_out), .C(CLK_t), .en(or_2_out), .Q(Branching_SetUp_q));
  Demultiplexer #(.Selector_Bits(2)) demultiplexer_1 (
    .sel(EX_Do_SMTH), .in(EX_NO_NOP), .out_0(EX_Jump_EN), .out_1(EX_Math_EN), .out_2(EX_Mem_EN),
    .out_3(EX_Mov_EN));
  Multiplexer #(.Bits(8)) multiplexer_1 (.sel(EX_Mov_EN), .in_0(EX_ALU_Out), .in_1(EX_Data_B), .out(multiplexer_1_out));
  Register #(.Bits(3)) register_1 (.D(EX_ME_Out[18:16]), .C(CLK_t), .en(1'b1), .Q(register_1_q));
  Multiplexer #(.Bits(8)) multiplexer_2 (
    .sel(ME_Do_RD), .in_0(R_Src_2_Out), .in_1(Input_8Bits), .out(multiplexer_2_out));
  Counter #(.Bits(2)) counter_1 (
    .en(Branching_SetUp_q), .C(CLK_t), .clr(comparator_1_eq), .out(counter_1_out));  // open: ovf
  not not_1 (EX_NO_NOP, ID_EX_Out[24]);
  and and_1 (and_1_out, CLK_t, EX_NO_NOP);
  Demultiplexer #(.Bits(3)) demultiplexer_2 (
    .sel(ME_Do_WR), .in(register_1_q), .out_0(ME_R_DestOut), .out_1(ME_R_Src2));
  Register #(.Bits(16)) register_2 (.D(EX_ME_Forward_Out), .C(CLK_t), .en(1'b1), .Q({LD_ST_CMD[7:0], LD_ST_CMD[15:8]}));
  and and_2 (LD_ST_CMD[17], CLK_t, EX_ME_Out[20]);
  assign not_2_out = ~EX_Do_SMTH;  // Not not_2, 2 bits wide
  Register #(.Bits(8)) register_3 (.D(multiplexer_2_out), .C(CLK_t), .en(EX_ME_Out[24]), .Q(register_3_q));
  ROM #(.AddrBits(8), .Bits(20)) Instruction (.A(out_4), .sel(NotNOPing), .D(Instruction_d));
  Multiplexer multiplexer_3 (.sel(comparator_1_eq), .in_0(Branching_SetUp_q), .in_1(1'b0), .out(multiplexer_3_out));
  Comparator #(.Bits(2)) comparator_1 (.a(counter_1_out), .b(2'b10), .eq(comparator_1_eq));  // open: gt, lt
  assign not_3_out = ~not_2_out;  // Not not_3, 2 bits wide
  Demultiplexer #(.Bits(8)) demultiplexer_3 (
    .sel(ME_Do_RD), .in(register_3_q), .out_0(Output_8Bits), .out_1(ME_RD_WR_output));
  forward_register forward_register_1 (
    .Data_PostEX(multiplexer_1_out), .R_Dest_In(EX_R_Dest), .Do_SMTH(not_3_out), .CLK(and_1_out),
    .Data_1(EX_Data_A), .Data_2(EX_Data_B), .R_Src1(EX_R_Src1), .R_Src2(EX_R_Src2), .IMM_Check(EX_IMM_check),
    .Out_1(EX_Forward_A), .Out_2(EX_Forward_B), .DBG1(out_10), .DBG2(out_11), .DBG3(out_12));
  not not_4 (not_4_out, comparator_1_eq);
  Comparator #(.Bits(2)) comparator_2 (.a(EX_Do_SMTH), .b(2'b10), .eq(comparator_2_eq));  // open: gt, lt
  Comparator #(.Bits(2)) comparator_3 (.a(multiplexer_4_out), .b(2'b01), .gt(EX_DO_Stack));  // open: eq, lt
  Demultiplexer #(.Selector_Bits(2)) demultiplexer_4 (
    .sel(EX_ME_Out[20:19]), .in(EX_ME_Out[24]), .out_0(ME_Do_WR), .out_1(ME_Do_RD), .out_2(LD_ST_CMD[18]),
    .out_3(LD_ST_CMD[16]));
  Multiplexer #(.Bits(2)) multiplexer_4 (
    .sel(comparator_2_eq), .in_0(2'b00), .in_1({1'b1, EX_ALU_Choice_01[0]}), .out(multiplexer_4_out));
  Register #(.Bits(20)) IF_ID (
    .D(Instruction_d), .C(CLK_t), .en(1'b1),
    .Q({ID_Opcode, ID_IMM_check, ID_R_Dest, ID_R_Src1, ID_R_Src2_IMM, ID_R_Src2}));
  Multiplexer #(.Bits(19)) multiplexer_5 (
    .sel(EX_ME_Out[21]), .in_0(LD_ST_CMD),
    .in_1({LD_ST_CMD[18], PSH_POP_CMD[17], LD_ST_CMD[16], PSH_POP_CMD[15:0]}), .out(multiplexer_5_out));
  and and_3 (and_3_out, EX_Jump_EN, EX_NO_NOP);
  Register #(.Bits(16)) register_4 (.D(EX_ME_Forward_Out), .C(CLK_t), .en(1'b1), .Q({PSH_POP_CMD[15:8], register_4_q}));
  and and_4 (PSH_POP_CMD[17], CLK_t, EX_ME_Out[20]);
  not not_5 (not_5_out, EX_Reg_F[3]);
  Multiplexer multiplexer_6 (.sel(and_3_out), .in_0(1'b0), .in_1(EX_Do_Jump), .out(EX_Do_Branch_Taking));
  not not_6 (not_6_out, multiplexer_5_out[16]);
  not not_7 (not_7_out, multiplexer_5_out[18]);
  Comparator #(.Bits(8)) comparator_4 (.a(8'h8), .b(ID_StackPtr_Out), .lt(comparator_4_lt));  // open: gt, eq
  Multiplexer #(.Selector_Bits(2)) multiplexer_7 (
    .sel(EX_ALU_Choice_01[1:0]), .in_0(EX_Reg_F[0]), .in_1(EX_Reg_F[3]), .in_2(not_5_out),
    .in_3(EX_Reg_F[2]), .out(multiplexer_7_out));
  not not_8 (not_8_out, EX_Do_Jump);
  Demultiplexer demultiplexer_5 (.sel(EX_ME_Out[21]), .in(LD_ST_CMD[18]), .out_0(ME_Do_LD), .out_1(ME_Do_POP));
  Demultiplexer demultiplexer_6 (.sel(EX_ME_Out[21]), .in(LD_ST_CMD[16]), .out_0(ME_Do_ST), .out_1(ME_Do_PSH));
  not not_9 (not_9_out, not_6_out);
  not not_10 (not_10_out, not_7_out);
  assign PSH_POP_CMD[7:0] = ~EX_ME_Stack_Addr;  // Not not_11, 8 bits wide
  not not_12 (Stack_OVERSIZE, comparator_4_lt);
  and and_5 (and_5_out, not_8_out, and_3_out);
  RAMDualPort #(.AddrBits(8), .Bits(8)) ramdualport_1 (
    .A(multiplexer_5_out[7:0]), .Din(multiplexer_5_out[15:8]), .str(not_9_out), .C(multiplexer_5_out[17]),
    .ld(not_10_out), .D(ME_LD_ST_output));
  Register #(.Bits(8)) Stack (.D(EX_ALU_Out), .C(CLK_t), .en(EX_Mem_EN), .Q(ID_StackPtr_Out));
  Comparator #(.Bits(8)) comparator_5 (.a({8{1'b0}}), .b(ID_StackPtr_Out), .eq(Stack_EMPTY));  // open: gt, lt
  or or_4 (EX_Do_Jump, multiplexer_7_out, EX_ALU_Choice_01[2]);
  Multiplexer multiplexer_8 (.sel(and_5_out), .in_0(not_13_out), .in_1(EX_Jump_EN), .out(multiplexer_8_out));
  not not_13 (not_13_out, EX_NO_NOP);
  Multiplexer #(.Bits(16)) multiplexer_9 (
    .sel(EX_Math_EN), .in_0({8'h1, ID_EX_Stack_Out[7:0]}), .in_1({EX_Forward_B, EX_Forward_A}),
    .out(multiplexer_9_out));
  Multiplexer #(.Bits(3)) multiplexer_10 (
    .sel(EX_Math_EN), .in_0(EX_ALU_Choice_10), .in_1(EX_ALU_Choice_01), .out(multiplexer_10_out));
  not not_14 (not_14_out, NotNOPing);
  or or_5 (EX_NOP_Out, EX_Do_Branch_Taking, multiplexer_8_out);
  Register register_5 (.D(EX_ME_Out[24]), .C(CLK_t), .en(1'b1), .Q(register_5_q));
  Register register_6 (.D(not_14_out), .C(CLK_t), .en(1'b1), .Q(register_6_q));
  ALU ALU (
    .A(multiplexer_9_out[7:0]), .B(multiplexer_9_out[15:8]), .Do_Math(multiplexer_10_out), .Res(ALU_res),
    .C_F(ALU_c_f[0]), .O_F(ALU_c_f[1]), .N_F(ALU_c_f[2]), .Z_F(ALU_c_f[3]));
  Multiplexer #(.Bits(8)) multiplexer_11 (
    .sel(EX_ME_Out[19]), .in_0(EX_ME_Stack_Out), .in_1(EX_ME_Stack_Out), .out(EX_ME_Stack_Addr));
  Multiplexer #(.Bits(5)) multiplexer_12 (.sel(or_6_out), .in_0(ID_Opcode), .in_1({5{1'b0}}), .out(multiplexer_12_out));
  or or_6 (or_6_out, not_14_out, register_6_q);
  and and_6 (and_6_out, EX_Math_EN, EX_NO_NOP);
  and and_7 (and_7_out, WB_NO_NOP, ME_WB_Out[12]);
  Multiplexer #(.Selector_Bits(2), .Bits(8)) multiplexer_13 (
    .sel(EX_Do_SMTH), .in_0({8{1'b0}}), .in_1(EX_ALU_Out), .in_2({8{1'b0}}), .in_3(EX_Data_B),
    .out(multiplexer_13_out));
  not not_15 (not_15_out, EX_DO_Stack);
  Multiplexer #(.Bits(3)) multiplexer_14 (
    .sel(register_5_q), .in_0(ID_R_Src2), .in_1(ME_R_Src2), .out(multiplexer_14_out));
  Multiplexer #(.Bits(8)) multiplexer_15 (.sel(not_15_out), .in_0({8{1'b0}}), .in_1(ALU_res), .out(EX_ALU_Out));
  Register #(.Bits(4)) register_7 (.D(ALU_c_f), .C(CLK_t), .en(and_6_out), .Q(EX_Reg_F));
  ROM #(.AddrBits(5), .Bits(6)) rom_1 (.A(multiplexer_12_out), .sel(1'b1), .D(rom_1_d));
  Multiplexer #(.Bits(8)) multiplexer_16 (
    .sel(ID_IMM_check), .in_0(R_Src_2_Out), .in_1({ID_R_Src2_IMM, ID_R_Src2}), .out(ID_Data_B));
  not not_16 (not_16_out, EX_Do_Jump);
  RegisterFile #(.AddrBits(3), .Bits(8)) RegFile (
    .Din(ME_WB_Out[7:0]), .we(and_7_out), .Rw(ME_WB_Out[10:8]), .C(CLK_t), .Ra(ID_R_Src1),
    .Rb(multiplexer_14_out), .Da(ID_Data_A), .Db(R_Src_2_Out));
  Register register_8 (.D(not_16_out), .C(CLK_t), .en(1'b1), .Q(register_8_q));
  Comparator #(.Bits(2)) comparator_6 (.a(EX_Do_SMTH), .b(2'b10), .eq(comparator_6_eq));  // open: gt, lt
  Register register_9 (.D(EX_ME_Out[25]), .C(CLK_t), .en(1'b1), .Q(register_9_q));
  Multiplexer #(.Bits(3)) multiplexer_17 (
    .sel(EX_ALU_Choice_01[0]), .in_0(3'b001), .in_1(3'b000), .out(EX_ALU_Choice_10));
  Multiplexer multiplexer_18 (.sel(or_7_out), .in_0(EX_ME_Out[25]), .in_1(register_9_q), .out(ME_DelayNOP));
  or or_7 (or_7_out, register_8_q, register_10_q);
  Register register_10 (.D(register_8_q), .C(CLK_t), .en(1'b1), .Q(register_10_q));
  Multiplexer #(.Bits(26)) multiplexer_19 (
    .sel(comparator_6_eq),
    .in_0({EX_NOP_Out, 1'b0, EX_Do_SMTH, EX_ALU_Choice_01, EX_R_Dest, {8{1'b0}}, multiplexer_13_out}),
    .in_1({EX_NOP_Out, 1'b1, EX_Do_SMTH, EX_ALU_Choice_01, EX_R_Dest, EX_Data_A, EX_Data_B}),
    .out(multiplexer_19_out));
  or or_8 (or_8_out, ME_Do_LD, ME_Do_POP);
  Register #(.Bits(26)) register_11 (.D(EX_ME_Out), .C(CLK_t), .en(1'b1), .Q(register_11_q));
  Register register_12 (.D(EX_ME_Out[24]), .C(CLK_t), .en(1'b1), .Q(register_12_q));
  Multiplexer #(.Bits(8)) multiplexer_20 (
    .sel(EX_ME_Out[20]), .in_0(ME_RD_WR_output), .in_1(ME_LD_ST_output), .out(multiplexer_20_out));
  not not_17 (WB_NO_NOP, ME_WB_Out[11]);
  Multiplexer multiplexer_21 (
    .sel(EX_ME_Out[21]), .in_0(EX_ME_Out[24]), .in_1(register_12_q), .out(multiplexer_21_out));
  Multiplexer #(.Bits(12)) multiplexer_22 (
    .sel(not_19_out), .in_0({ME_DelayNOP, EX_ME_Out[18:16], multiplexer_20_out}),
    .in_1({register_11_q[25], ME_R_DestOut, register_11_q[7:0]}), .out(ME_WB_Out[11:0]));
  not not_18 (not_18_out, multiplexer_21_out);
  Register #(.Bits(9)) ID_EX_Stack (.D({Stack_EMPTY, ID_StackPtr_Out}), .C(CLK_t), .en(1'b1), .Q(ID_EX_Stack_Out));
  Register #(.Bits(32)) ID_EX (
    .D({ID_IMM_check, ID_R_Src2, ID_R_Src1, rom_1_d, ID_R_Dest, ID_Data_A, ID_Data_B}), .C(CLK_t), .en(1'b1),
    .Q({EX_IMM_check, EX_R_Src2, EX_R_Src1, ID_EX_Out[24], EX_Do_SMTH, EX_ALU_Choice_01, EX_R_Dest, EX_Data_A, EX_Data_B}));
  Register #(.Bits(26)) EX_ME (.D(multiplexer_19_out), .C(CLK_t), .en(1'b1), .Q(EX_ME_Out));
  Register #(.Bits(16)) EX_ME_Forward (.D({EX_Forward_B, EX_Forward_A}), .C(CLK_t), .en(1'b1), .Q(EX_ME_Forward_Out));
  Register #(.Bits(8)) EX_ME_Stack (.D(ID_EX_Stack_Out[7:0]), .C(CLK_t), .en(1'b1), .Q(EX_ME_Stack_Out));
  not not_19 (not_19_out, register_12_q);
  or or_9 (ME_WB_Out[12], not_18_out, or_8_out);

  assign out_5 = out_4;
  assign out_6 = out_4;

  // Other names for the same wires on the sheet: ID_R_Src2_IMM[2:0] = ID_R_Src2; WB_output[7:0] = ME_WB_Out[7:0];
  //   WB_R_Dest[2:0] = ME_WB_Out[10:8]; WB_EN = ME_WB_Out[12]; CLK_Lower = in_7; CLK_Middle = in_8; CLK_Upper = in_9;
  //   ME_Data_B[7:0] = EX_ME_Out[7:0]; ME_Data_A[7:0] = EX_ME_Out[15:8]; ME_R_Dest[2:0] = EX_ME_Out[18:16];
  //   ME_SMTH_Choice[2:0] = EX_ME_Out[21:19]; ME_RAM_EN = EX_ME_Out[20]; PSH_POP_EN = EX_ME_Out[21];
  //   ME_Do_smth[1:0] = EX_ME_Out[23:22]; ME_EN = EX_ME_Out[24]; ME_NOP = EX_ME_Out[25]; RegF_C = EX_Reg_F[0];
  //   RegF_O = EX_Reg_F[1]; RegF_N = EX_Reg_F[2]; RegF_Z = EX_Reg_F[3]; EX_StackPtr_Update = EX_Mem_EN;
  //   EX_MOV_Out[7:0] = EX_Data_B;
  //   ID_EX_Out (some bits) = {EX_IMM_check, EX_R_Src2, EX_R_Src1, EX_Do_SMTH, EX_ALU_Choice_01, EX_R_Dest, EX_Data_A, EX_Data_B};
  //   Line_Branch[7:0] = EX_Data_B; EX_SMTH_Choice[2:0] = EX_ALU_Choice_01; ID_Stack_EMPTY = Stack_EMPTY;
  //   ID_Stack_OVERSIZE = Stack_OVERSIZE; in_8bit[7:0] = Input_8Bits; ME_Do_LD_POP = LD_ST_CMD[18];
  //   PSH_POP_CMD (some bits) = {LD_ST_CMD[18], LD_ST_CMD[16]}; ME_Do_ST_PSH = LD_ST_CMD[16];
  //   out_8bits[7:0] = Output_8Bits; PC_Out[7:0] = out_4

  // Notes on the sheet:
  //   Program Counter
  //   Pipeline Stages
  //   Instruction Fetch
  //   Execute
  //   Memory
  //   Branch Prediction
  //   Static Guess Not Taken Branch
  //   Data Forwarding Register
  //   Do_{I/O}
  //   Do_{LD/ST}
  //   Might be problem here
  //   Sol: change to 2 bits
  //   and detect for 10
  //   Opcode
  //   0000: LD
  //   0001: MOV
  //   0010: ST
  //   0011: RD
  //   0100: ADD
  //   0101L SUB
  //   0110: MUL
  //   0111: WR
  //   1000: AND
  //   1001: OR
  //   1010: XOR
  //   1011: NOT
  //   1100: BC
  //   1101:BZ
  //   1110: BNZ
  //   1111:B
  //   contents of Instruction (hex, n*v repeats v):
  //   f4011,f482f,21100,29900,ec364,e4864,36105,5a804,43504,2e464,9c00c
  //   ,a4009,f78ff
  //   IF/ID
  //   Do_{SMTH}: 10
  //   SMTH_{Choice}:
  //   000: RD
  //   001: WR
  //   Do_{SMTH}: 10
  //   SMTH_{Choice}:
  //   010: LD
  //   011: ST
  //   Do_{Jump}
  //   Do_{PSH/POP}
  //   Do_{SMTH}: 00
  //   SMTH_{Choice}:
  //   000: BC
  //   001: BZ
  //   010: BNZ
  //   011: BNG
  //   100: B
  //   PSH: IN -> ChangePTR
  //   POP ChangePTR -> OUT
  //   Do_{Math}
  //   Do_{SMTH}: 01
  //   SMTH_{Choice}:
  //   000: ADD
  //   001: SUB
  //   010: MUL
  //   011: DC
  //   100:: AND
  //   101: Or
  //   110: XOR
  //   111: Not
  //   Instruction Decode
  //   Check if Stack is too big
  //   PC_{Out}
  //   CU
  //   NOP: [5]
  //   1: True
  //   0: False
  //   Do_{SMTH}: [4:3]
  //   00 Do_{Jump} (In:EX)
  //   01 Do_{Math}(In:EX -> WB)
  //   10 Do_{Mem} (In:ME -> WB)
  //   11 Do_{Mov} (In:WB)
  //   SMTH_{Choice}: [2:0]
  //   Do_{SMTH}: 10
  //   SMTH_{Choice}:
  //   110: POP
  //   111: PSH
  //   contents of rom_1 (hex, n*v repeats v):
  //   4*20,8,9,a,20,c,d,e,f,4*20,0,1,2,3,4,20,17,16,10,11,20,20,12,13
  //   ,18,20
  //   ME/WB
  //   Write Back
  //   Do_{Mem}
  //   Do_{SMTH}: 10
  //   SMTH_{Choice}:
  //   110: PSH
  //   111: POP
  //   ID/EX
  //   EX/ME
endmodule
