// Digital circuit D_flip_flop.dig as structural Verilog
module D_flip_flop (
  input  D,
  input  CLK,
  output Q,
  output Q_2
);

  wire nand_1_out, nand_2_out, nand_3_out;

  nand nand_1 (nand_1_out, D, D);
  nand nand_2 (nand_2_out, D, CLK);
  nand nand_3 (nand_3_out, CLK, nand_1_out);
  nand nand_4 (Q, nand_2_out, Q_2);
  nand nand_5 (Q_2, Q, nand_3_out);
endmodule
