// Digital circuit TEMP.dig as structural Verilog
module TEMP (
);

  wire CLK, EX_Do_Jump, ME_DelayNOP, ME_Do_LD, ME_Do_POP, ME_EN, ME_NOP, multiplexer_3_out, not_1_out,
       not_2_out, not_3_out, or_1_out, or_2_out, PSH_POP_EN, register_1_q, register_2_q, register_3_q,
       register_5_q;
  wire [1:1] ME_SMTH_Choice;
  wire [2:0] ME_R_Dest, ME_R_Dest_Out;
  wire [7:0] ME_LD_ST_output, ME_RD_WR_output, multiplexer_2_out;
  wire [12:0] ME_WB_Out;
  wire [25:0] EX_ME_Out, register_4_q;

  not not_1 (not_1_out, EX_Do_Jump);
  Register register_1 (.D(not_1_out), .C(CLK), .en(1'b1), .Q(register_1_q));
  Register register_2 (.D(ME_NOP), .C(CLK), .en(1'b1), .Q(register_2_q));
  Multiplexer multiplexer_1 (.sel(or_1_out), .in_0(ME_NOP), .in_1(register_2_q), .out(ME_DelayNOP));
  or or_1 (or_1_out, register_1_q, register_3_q);
  Register register_3 (.D(register_1_q), .C(CLK), .en(1'b1), .Q(register_3_q));
  or or_2 (or_2_out, ME_Do_LD, ME_Do_POP);
  Register #(.Bits(26)) register_4 (.D(EX_ME_Out), .C(CLK), .en(1'b1), .Q(register_4_q));
  Register register_5 (.D(ME_EN), .C(CLK), .en(1'b1), .Q(register_5_q));
  Multiplexer #(.Bits(8)) multiplexer_2 (
    .sel(ME_SMTH_Choice[1]), .in_0(ME_RD_WR_output), .in_1(ME_LD_ST_output), .out(multiplexer_2_out));
  Multiplexer multiplexer_3 (.sel(PSH_POP_EN), .in_0(ME_EN), .in_1(register_5_q), .out(multiplexer_3_out));
  Multiplexer #(.Bits(12)) multiplexer_4 (
    .sel(not_3_out), .in_0({ME_DelayNOP, ME_R_Dest, multiplexer_2_out}),
    .in_1({register_4_q[25], ME_R_Dest_Out, register_4_q[7:0]}), .out(ME_WB_Out[11:0]));
  not not_2 (not_2_out, multiplexer_3_out);
  not not_3 (not_3_out, register_5_q);
  or or_3 (ME_WB_Out[12], not_2_out, or_2_out);
endmodule
