// Digital circuit flag_register.dig as structural Verilog
module flag_register (
  input  [3:0] CONZ_i,
  input  Do_Write,
  output [3:0] CONZ_o
);

  D_flip_flop d_flip_flop_1 (.D(CONZ_i[0]), .CLK(Do_Write), .Q(CONZ_o[0]));  // open: Q_2
  D_flip_flop d_flip_flop_2 (.D(CONZ_i[1]), .CLK(Do_Write), .Q(CONZ_o[1]));  // open: Q_2
  D_flip_flop d_flip_flop_3 (.D(CONZ_i[2]), .CLK(Do_Write), .Q(CONZ_o[2]));  // open: Q_2
  D_flip_flop d_flip_flop_4 (.D(CONZ_i[3]), .CLK(Do_Write), .Q(CONZ_o[3]));  // open: Q_2
endmodule
