// Digital circuit full_adder.dig as structural Verilog
module full_adder (
  input  A,
  input  B,
  input  C_i,
  output S,
  output C_o
);

  wire half_adder_1_c_o, half_adder_1_s, half_adder_2_c_o;

  half_adder half_adder_1 (.A(A), .B(B), .S(half_adder_1_s), .C_o(half_adder_1_c_o));
  half_adder half_adder_2 (.A(half_adder_1_s), .B(C_i), .S(S), .C_o(half_adder_2_c_o));
  or or_1 (C_o, half_adder_2_c_o, half_adder_1_c_o);
endmodule
