// Digital circuit multiply_check_helper.dig as structural Verilog
module multiply_check_helper (
  input  [7:0] A,
  input  B,
  output [7:0] Out
);

  and and_1 (Out[0], A[0], B);
  and and_2 (Out[1], A[1], B);
  and and_3 (Out[2], A[2], B);
  and and_4 (Out[3], A[3], B);
  and and_5 (Out[4], A[4], B);
  and and_6 (Out[5], A[5], B);
  and and_7 (Out[6], A[6], B);
  and and_8 (Out[7], A[7], B);
  // Pins of 1 and 8 bits meet at A
  // Pins of 1 and 8 bits meet at Out
endmodule
