// Digital circuit multiplier.dig as structural Verilog
module multiplier (
  input  [7:0] B,
  input  [7:0] A,
  input  CLK,
  output [7:0] M,
  output O_F
);

  wire comparator_1_eq, not_1_out, or_1_out;
  wire [7:0] _8bits_adder_1_s, counter_1_out, demultiplexer_1_out_1, multiplexer_1_out, register_1_q;

  or or_1 (or_1_out, B[0], B[1], B[2], B[3], B[4], B[5], B[6], B[7]);
  Comparator #(.Bits(8)) comparator_1 (.a(A), .b(counter_1_out), .eq(comparator_1_eq));  // open: gt, lt
  Counter #(.Bits(8)) counter_1 (.en(or_1_out), .C(CLK), .clr(comparator_1_eq), .out(counter_1_out));  // open: ovf
  _8bits_adder _8bits_adder_1 (.A(B), .B(demultiplexer_1_out_1), .C(1'b0), .S(_8bits_adder_1_s));  // open: C_o
  Multiplexer #(.Bits(8)) multiplexer_1 (
    .sel(comparator_1_eq), .in_0(_8bits_adder_1_s), .in_1({8{1'b0}}), .out(multiplexer_1_out));
  Demultiplexer #(.Bits(8)) demultiplexer_1 (
    .sel(not_1_out), .in(register_1_q), .out_0(M), .out_1(demultiplexer_1_out_1));
  not not_1 (not_1_out, comparator_1_eq);
  Comparator #(.Bits(8)) comparator_2 (.a(register_1_q), .b(multiplexer_1_out), .gt(O_F));  // open: eq, lt
  Register #(.Bits(8)) register_1 (.D(multiplexer_1_out), .C(CLK), .en(1'b1), .Q(register_1_q));

  // Notes on the sheet:
  //   B: default 15
  //   A: default 5
endmodule

/* Test case:
A B M
0 1 0
1 0 0
1 2 2
2 1 2
2 2 4
5 6 30
*/
